# Fritzing sketch Homekit (saved by Fritzing 0.9.4)
breadboards: 1

parts:
  SparkFun_ESP32_Thing_Plus = SparkFun ESP32 Thing Plus [part_number=14689]
  BME280 = BME280 Breakout
  Bauteil1 = NRF24L01+ Breakout Board
  U7 = RF-LINK_TX [package=rf-link_tx]

nets:
  N1: SparkFun_ESP32_Thing_Plus.27, U7.DATA
  N2: SparkFun_ESP32_Thing_Plus.33, Bauteil1.CE
  N3: SparkFun_ESP32_Thing_Plus.SCL, BME280.SCK/SCL
  N4: SparkFun_ESP32_Thing_Plus.SDA, BME280.SDI/SDA
  3.3V: SparkFun_ESP32_Thing_Plus.3.3V, BME280.3.3V, Bauteil1.VCC, U7.+5V
  GND: SparkFun_ESP32_Thing_Plus.GND, BME280.GND, Bauteil1.GND, U7.GND
  N5: SparkFun_ESP32_Thing_Plus.SCK, Bauteil1.SCK
  N6: SparkFun_ESP32_Thing_Plus.MOSI, Bauteil1.MOSI
  N7: SparkFun_ESP32_Thing_Plus.MISO, Bauteil1.MISO

custom parts:
  SparkFun ESP32 Thing Plus: The SparkFun ESP32 Thing Plus enjoys all the amenities of the ESP32 Thing, but with a few added sparkles. We've lengthened the board just a bit to accommodate a Qwiic connector for all your Qwiic breakout needs. We've also moved a few pins around to make the board compatible with the Adafruit Huzzah32 – ESP32 Feather Board such that you can use all of those lovely shields available out there!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
  RF-LINK_TX: Common RF transmitter of the 315.00Mhz varity
