# Fritzing sketch ATTiny85_NRF24_BME280_SPI (saved by Fritzing 0.9.4)
breadboards: 1

parts:
  ATTiny85 = attiny85 [package=dip]
  NRF24 = NRF24L01+ Breakout Board
  BME280_SPI = BME280 Breakout

nets:
  CS BME280: ATTiny85.Pin_2, BME280_SPI.!CS
  CS RF24: ATTiny85.Pin_3, NRF24.CS
  GND: ATTiny85.Pin_4, NRF24.GND, BME280_SPI.GND
  MOSI: ATTiny85.Pin_5, NRF24.MOSI, BME280_SPI.SDI/SDA
  MISO: ATTiny85.Pin_6, NRF24.MISO, BME280_SPI.SDO/ADR
  SCK: ATTiny85.Pin_7, NRF24.SCK, BME280_SPI.SCK/SCL
  3.3V: ATTiny85.Pin_8, NRF24.VCC, NRF24.CE, BME280_SPI.3.3V
