# Fritzing sketch nRF24L01+(With Socket) Attiny85 (saved by Fritzing 0.9.4)
breadboards: 1

parts:
  U1 = attiny85 [package=dip]
  1n4148 = Diode [package=diode-1n4148]
  22kΩ = Resistor [tolerance=±5% resistance=22k package=THT]
  10nF = Ceramic Capacitor [capacitance=10nF package="100 mil [THT, multilayer]"]
  VCC1 = Battery
  nRF24L01+ = NRF24L01+ Breakout Board

nets:
  N1: U1.Pin_4, 10nF.0, VCC1.-, nRF24L01+.GND
  N2: U1.Pin_5, nRF24L01+.MISO
  N3: U1.Pin_6, nRF24L01+.MOSI
  N4: U1.Pin_7, 1n4148.C, nRF24L01+.SCK
  N5: U1.Pin_8, 22kΩ.Pin_0, VCC1.+, nRF24L01+.VCC, nRF24L01+.CE
  N6: 1n4148.A, 22kΩ.Pin_1, 10nF.1, nRF24L01+.CS
